# Fritzing sketch project phase 1 (saved by Fritzing 1.0.5)
stripboards: 6

parts:
  M1 = DC Motor [voltage_(max)=6V voltage_(min)=3V]
  M2 = DC Motor [voltage_(max)=6V voltage_(min)=3V]
  M3 = DC Motor [voltage_(max)=6V voltage_(min)=3V]
  M4 = DC Motor [voltage_(max)=6V voltage_(min)=3V]
  Part2 = Bluetooth HC-05 Macho
  R1 = Photocell (LDR) [power=0.5W dark_resistance_@0.01lx=0.3MΩ light_resistance_@100lx=400Ω luminance=10lx package=THT]  # not connected
  U1 = LCD-16X2 [package=lcd-16x2_nosilk]
  LED2 = smd LED [color="Red (633nm)" package="0805 [SMD]"]
  LED3 = smd LED [color="Red (633nm)" package="0805 [SMD]"]
  R2 = Rotary Potentiometer (Large) [maximum_resistance=50kΩ knob_status=50% power=0.5W package=THT]
  U4 = LIPO-110mAh [package=lipo-110]
  U5 = LIPO-110mAh [package=lipo-110]
  U6 = LIPO-110mAh [package=lipo-110]
  U3 = LIPO-110mAh [package=lipo-110]
  L298N1 = L298N DC motor driver
  HC-SR04_Sensor_1 = HC-SR04 Ultrasonic Distance Sensor
  LED6 = smd LED [color="White (4500K)" package="0805 [SMD]"]
  LED5 = smd LED [color="White (4500K)" package="0805 [SMD]"]
  Part1 = Arduino Uno (Rev3)
  Mod1 = KY-018 Photoresistor Module [package="Breakout board"]

nets:
  N1: M1.pin_1, M2.pin_1, L298N1.OUT3
  N2: M1.pin_2, M2.pin_2, L298N1.OUT4
  N3: M3.pin_1, M4.pin_1, L298N1.OUT2
  N4: M3.pin_2, M4.pin_2, L298N1.OUT1
  N5: Part2.TXD, Part1.D0/RX
  N6: Part2.RXD, Part1.D1/TX
  VCC: Part2.VCC, U1.VDD, U1.A, R2.leg2, HC-SR04_Sensor_1.VCC, Part1.5V, Mod1.Vin
  GND: Part2.GND, U1.VSS, U1.R_W, U1.K, LED2.cathode, LED3.cathode, R2.leg1, U3.-, L298N1.GND, HC-SR04_Sensor_1.GND, LED6.cathode, LED5.cathode, Part1.GND, Mod1.-
  N7: U1.VO, R2.wiper
  N8: U1.RS, Part1.A1
  N9: U1.E, Part1.A2
  N10: U1.DB4, Part1.A3
  N11: U1.DB5, Part1.A4/SDA
  N12: U1.DB6, Part1.A5/SCL
  N13: U1.DB7, Part1.D13/SCK
  N14: LED2.anode, LED3.anode, Part1.D10_PWM/SS
  N15: U4.+, U5.-
  N16: U4.-, U3.+
  N17: U5.+, U6.-
  12V: U6.+, L298N1.12V, Part1.VIN
  N18: L298N1.ENA, Part1.D3_PWM
  N19: L298N1.ENB, Part1.D9_PWM
  N20: L298N1.IN1, Part1.D5_PWM
  N21: L298N1.IN2, Part1.D4
  N22: L298N1.IN3, Part1.D7
  N23: L298N1.IN4, Part1.D6_PWM
  N24: HC-SR04_Sensor_1.TRIG, Part1.D12/MISO
  N25: HC-SR04_Sensor_1.ECHO, Part1.D8
  N26: LED6.anode, LED5.anode, Part1.D11_PWM/MOSI
  N27: Part1.A0, Mod1.S

custom parts:
  L298N DC motor driver: 2x DC motor driver with 78M05 positive voltage regulator (7..35 V) L298N: max 46 V, 2 A Set 5 V Enable jumper to enable 5 V regultor (needed for the L298N) and +5 V output at screw terminal or supply external +5 V at screw terminal Set ENA and/or ENB to +5 V to enable motor permanently or supply ENA and/or ENB with PWM signal IN1 and IN2 set rotation directory for motor A (OUT1/OUT2) IN2 and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
  KY-018 Photoresistor Module: KY-018 Photoresistor module, used to measure light intensity. It can determine the presence or absence of light.

// code stored in the sketch: code.ino
/*
  ADAS Phase1 - Arduino Uno sketch
  Features implemented:
   - Bluetooth control via HC-05 (SoftwareSerial on D10/D11)
     * Commands supported (text commands from your RC app):
       S:<0-255>   -> set target speed PWM (accelerator)
       BRAKE       -> immediate braking (ramp down ignoring accelerator)
       STOP        -> immediate stop (same as BRAKE)
       FORWARD     -> full ahead (S:200)
       REVERSE     -> reverse/back (S:-200) [optional; not used by many RC apps]
       LEFT / RIGHT / STRAIGHT -> steering hints (not used in differential drive)
   - Motor control (L298N) using supplied pins
   - Ultrasonic HC-SR04-based TTC calculation and automatic deceleration
   - Ambient LDR-based headlight control (A0)
   - LCD 16x2 parallel (4-bit mode) using your pin layout
   - Smooth ramping for acceleration & braking
   - Status LEDs/backlight simple support (backlight is 5V via resistor)
  
  Wiring references (from your confirmed mapping):
    LCD: RS=A1, E=A2, D4=A3, D5=A4, D6=A5, D7=D13, RW=GND, VO=pot wiper
    HC-05: HC_TX -> Arduino D10 (SoftwareSerial RX pin)
           HC_RX -> Arduino D11 (SoftwareSerial TX pin) [use level divider if desired]
    Ultrasonic: TRIG=D12, ECHO=D8
    LDR: A0
    Headlight LED: D2 (through 220R resistor) -> LED -> GND
    L298N:
      IN1 -> D5
      IN2 -> D4
      ENA -> D3 (PWM)  // left
      IN3 -> D7
      IN4 -> D6
      ENB -> D9 (PWM)  // right
*/

#include <LiquidCrystal.h>
#include <SoftwareSerial.h>

// ---------- PIN DEFINITIONS ----------
const int LCD_RS = A1;
const int LCD_E  = A2;
const int LCD_D4 = A3;
const int LCD_D5 = A4;
const int LCD_D6 = A5;
const int LCD_D7 = 13;

LiquidCrystal lcd(LCD_RS, LCD_E, LCD_D4, LCD_D5, LCD_D6, LCD_D7);

// Bluetooth (HC-05) using SoftwareSerial
const int BT_RX_PIN = 10; // Arduino receives from HC-05 TX on this pin
const int BT_TX_PIN = 11; // Arduino transmits to HC-05 RX on this pin
SoftwareSerial btSerial(BT_RX_PIN, BT_TX_PIN);

// Ultrasonic
const int TRIG_PIN = 12;
const int ECHO_PIN = 8;

// LDR
const int LDR_PIN = A0;
const int LDR_THRESHOLD = 500; // adjustable threshold, calibrate for your ambient levels

// Headlight
const int HEADLIGHT_PIN = 2;

// L298N Motor driver pins
const int L_IN1 = 5;
const int L_IN2 = 4;
const int L_ENA = 3; // PWM for left
const int R_IN3 = 7;
const int R_IN4 = 6;
const int R_ENB = 9; // PWM for right

// Debug LED (optional) - reuse D13? no, D13 is LCD D7. We'll not use another status LED here.

// ---------- CONTROL PARAMETERS ----------
int targetPWM = 0;          // target speed (0..255)
int currentPWM_left = 0;    // current output pwm for smoothing
int currentPWM_right = 0;

bool brakeRequested = false;

// Physics / calibration constants (VERY IMPORTANT: calibrate for your vehicle)
const float PWM_TO_MPS = 0.008f; 
// Explanation: estimated speed (m/s) = PWM * PWM_TO_MPS. 
// Example: pwm=125 -> ~1.0 m/s if PWM_TO_MPS = 0.008. Adjust experimentally.

const float DECELERATION = 0.6f; // m/s^2 - how fast the vehicle slows when braking (calibrate)
const float RAMP_STEP = 4;       // how many PWM units to change per ramp step
const unsigned long RAMP_DELAY_MS = 40; // ms between ramp steps

// Ultrasonic conversion
const float SOUND_SPEED = 343.0f; // m/s

unsigned long lastRampMillis = 0;

// ---------- SETUP ----------
void setup() {
  // pins
  pinMode(TRIG_PIN, OUTPUT);
  pinMode(ECHO_PIN, INPUT);
  pinMode(LDR_PIN, INPUT);
  pinMode(HEADLIGHT_PIN, OUTPUT);

  pinMode(L_IN1, OUTPUT);
  pinMode(L_IN2, OUTPUT);
  pinMode(L_ENA, OUTPUT);
  pinMode(R_IN3, OUTPUT);
  pinMode(R_IN4, OUTPUT);
  pinMode(R_ENB, OUTPUT);

  // Ensure motors stopped
  digitalWrite(L_IN1, LOW);
  digitalWrite(L_IN2, LOW);
  digitalWrite(R_IN3, LOW);
  digitalWrite(R_IN4, LOW);
  analogWrite(L_ENA, 0);
  analogWrite(R_ENB, 0);

  // Serials
  Serial.begin(9600);
  btSerial.begin(9600); // HC-05 default baud

  // LCD
  lcd.begin(16, 2);
  lcd.print("ADAS Phase 1");
  lcd.setCursor(0, 1);
  lcd.print("Init...");
  delay(1000);
  lcd.clear();

  // initial lights off
  digitalWrite(HEADLIGHT_PIN, LOW);
}

// ---------- MAIN LOOP ----------
void loop() {
  // 1) Bluetooth parse
  handleBluetooth();

  // 2) Read LDR & control headlights
  handleLights();

  // 3) Ultrasonic -> compute TTC and automatic decelerate if needed
  float distance_m = readUltrasonicDistance();
  float speed_mps = estimateSpeedMps((currentPWM_left + currentPWM_right) / 2.0f);
  float ttc = computeTTC(distance_m, speed_mps);

  // If braking is requested via BT, ramp down immediately (ignore target)
  if (brakeRequested) {
    // ramp down to zero
    rampToTarget(0);
    // keep braking flag until we reach zero
    if (currentPWM_left == 0 && currentPWM_right == 0) {
      brakeRequested = false;
    }
  } else {
    // Automatic safety: if TTC < stopping time, command deceleration
    float stopping_time = speed_mps / DECELERATION; // t = v/a
    if (speed_mps > 0.05 && ttc > 0 && ttc < stopping_time) {
      // reduce target gradually: set newTarget = max(0, targetPWM - some amount)
      int reducedTarget = max(0, (int)(targetPWM * 0.6f)); // conservative reduction, tune as needed
      targetPWM = reducedTarget;
    }
    // Ramp towards target
    rampToTarget(targetPWM);
  }

  // Update motors with current PWM & direction (we assume forward only for now)
  // If you want reverse: implement negative targetPWM handling and invert IN pins
  setMotorSpeed(currentPWM_left, currentPWM_right);

  // Update LCD
  updateLCD(speed_mps, distance_m, ttc);

  // Debug prints
  Serial.print("TargetPWM: "); Serial.print(targetPWM);
  Serial.print(" | CurL: "); Serial.print(currentPWM_left);
  Serial.print(" CurR: "); Serial.print(currentPWM_right);
  Serial.print(" | Dist(m): "); Serial.print(distance_m, 2);
  Serial.print(" | Speed(m/s): "); Serial.print(speed_mps, 2);
  Serial.print(" | TTC(s): "); Serial.println(ttc, 2);

  delay(100); // main loop delay (fine tune)
}

// ---------- BLUETOOTH HANDLING ----------
void handleBluetooth() {
  if (btSerial.available()) {
    String cmd = btSerial.readStringUntil('\n');
    cmd.trim();
    if (cmd.length() > 0) {
      parseCommand(cmd);
    }
  }

  // allow PC serial for debug input if desired
  if (Serial.available()) {
    String scmd = Serial.readStringUntil('\n');
    scmd.trim();
    if (scmd.length() > 0) parseCommand(scmd);
  }
}

void parseCommand(const String &cmd) {
  // Accept formats:
  //   S:<0-255>   -> speed
  //   BRAKE
  //   STOP
  //   FORWARD
  //   REVERSE
  //   LEFT, RIGHT, STRAIGHT (no-op for differential)
  String s = cmd;
  s.toUpperCase();

  if (s.startsWith("S:")) {
    // numeric speed
    int val = s.substring(2).toInt();
    val = constrain(val, 0, 255);
    targetPWM = val;
    brakeRequested = false;
  } else if (s == "BRAKE" || s == "STOP") {
    brakeRequested = true;
  } else if (s == "FORWARD") {
    targetPWM = 180; // arbitrary full-ish speed
    brakeRequested = false;
  } else if (s == "REVERSE") {
    // Reverse not fully implemented; for reverse you'd set direction pins accordingly
    // Here we treat REVERSE as braking then small reverse if you wire for it.
    targetPWM = 0;
    brakeRequested = true;
  } else if (s == "LEFT" || s == "RIGHT" || s == "STRAIGHT") {
    // Optional: steer via differential speed - not implemented by default
    // Could reduce right/left PWM to turn
  } else {
    // fallback: try to parse as plain number
    if (isDigits(s)) {
      int val = s.toInt();
      val = constrain(val, 0, 255);
      targetPWM = val;
      brakeRequested = false;
    }
  }
}

// helper: check if string is digits
bool isDigits(const String &str) {
  for (unsigned int i=0; i<str.length(); ++i) {
    if (!isDigit(str.charAt(i))) return false;
  }
  return true;
}

// ---------- ULTRASONIC ----------
float readUltrasonicDistance() {
  // returns distance in meters
  digitalWrite(TRIG_PIN, LOW);
  delayMicroseconds(2);
  digitalWrite(TRIG_PIN, HIGH);
  delayMicroseconds(10);
  digitalWrite(TRIG_PIN, LOW);

  unsigned long duration = pulseIn(ECHO_PIN, HIGH, 30000UL); // timeout ~30ms
  if (duration == 0) return -1.0f; // no reading

  float distance_m = (duration / 1e6f) * (SOUND_SPEED / 2.0f);
  return distance_m;
}

float computeTTC(float distance_m, float speed_mps) {
  if (distance_m <= 0 || speed_mps <= 0.01f) return 9999.0f;
  return distance_m / speed_mps;
}

// ---------- SPEED ESTIMATION & RAMPING ----------
float estimateSpeedMps(float pwmValue) {
  // Convert average PWM to estimated meters/second
  // MUST calibrate PWM_TO_MPS for your robot.
  if (pwmValue <= 0) return 0.0f;
  return pwmValue * PWM_TO_MPS;
}

void rampToTarget(int target) {
  unsigned long now = millis();
  if (now - lastRampMillis < RAMP_DELAY_MS) return;
  lastRampMillis = now;

  // Left
  if (currentPWM_left < target) {
    currentPWM_left = min(target, currentPWM_left + (int)RAMP_STEP);
  } else if (currentPWM_left > target) {
    currentPWM_left = max(target, currentPWM_left - (int)RAMP_STEP);
  }

  // Right (mirror)
  if (currentPWM_right < target) {
    currentPWM_right = min(target, currentPWM_right + (int)RAMP_STEP);
  } else if (currentPWM_right > target) {
    currentPWM_right = max(target, currentPWM_right - (int)RAMP_STEP);
  }
}

// ---------- MOTOR CONTROL ----------
void setMotorSpeed(int pwmLeft, int pwmRight) {
  // For now assume forward only. To support reverse, add sign handling and invert IN pins.
  // Left forward
  if (pwmLeft > 0) {
    digitalWrite(L_IN1, HIGH);
    digitalWrite(L_IN2, LOW);
    analogWrite(L_ENA, pwmLeft);
  } else {
    digitalWrite(L_IN1, LOW);
    digitalWrite(L_IN2, LOW);
    analogWrite(L_ENA, 0);
  }

  // Right forward
  if (pwmRight > 0) {
    digitalWrite(R_IN3, HIGH);
    digitalWrite(R_IN4, LOW);
    analogWrite(R_ENB, pwmRight);
  } else {
    digitalWrite(R_IN3, LOW);
    digitalWrite(R_IN4, LOW);
    analogWrite(R_ENB, 0);
  }
}

// ---------- LIGHTS & LCD ----------
void handleLights() {
  int ldr = analogRead(LDR_PIN);
  if (ldr < LDR_THRESHOLD) {
    digitalWrite(HEADLIGHT_PIN, HIGH);
  } else {
    digitalWrite(HEADLIGHT_PIN, LOW);
  }
}

void updateLCD(float speed_mps, float distance_m, float ttc) {
  lcd.setCursor(0, 0);
  lcd.print("Spd:");
  // print PWM-based speed as m/s with two decimals
  if (speed_mps < 0.001f) {
    lcd.print("0.00 m/s   ");
  } else {
    char buf0[16];
    dtostrf(speed_mps, 4, 2, buf0);
    lcd.print(buf0);
    lcd.print(" m/s");
  }

  lcd.setCursor(0, 1);
  // Lights state
  lcd.print(digitalRead(HEADLIGHT_PIN) ? "Lights:ON " : "Lights:OFF");
  lcd.print(" ");
  // TTC
  if (ttc > 999.0f) {
    lcd.print("TTC:---");
  } else {
    char buf1[10];
    dtostrf(ttc, 4, 2, buf1);
    lcd.print("TTC:");
    lcd.print(buf1);
  }
}

// ---------- END OF SKETCH ----------
